# Fritzing sketch radar (saved by Fritzing 0.9.3b)
circuit board: 5.19939cm x 5.21323cm
breadboards: 1

parts:
  LED1 = smd LED [color="Red (633nm)" package="0603 [SMD]"]
  LED2 = smd LED [color="Red (633nm)" package="0603 [SMD]"]
  LED3 = smd LED [color="Red (633nm)" package="0603 [SMD]"]
  LED4 = smd LED [color="Red (633nm)" package="0603 [SMD]"]
  LED5 = smd LED [color="Red (633nm)" package="0603 [SMD]"]
  LED6 = smd LED [color="Red (633nm)" package="0603 [SMD]"]
  LED7 = smd LED [color="Red (633nm)" package="0603 [SMD]"]
  LED8 = smd LED [color="Red (633nm)" package="0603 [SMD]"]
  LED9 = smd LED [color="Red (633nm)" package="0603 [SMD]"]
  LED10 = smd LED [color="Red (633nm)" package="0603 [SMD]"]
  LED11 = smd LED [color="Red (633nm)" package="0603 [SMD]"]
  LED12 = smd LED [color="Red (633nm)" package="0603 [SMD]"]
  LED13 = smd LED [color="Red (633nm)" package="0603 [SMD]"]
  LED14 = smd LED [color="Red (633nm)" package="0603 [SMD]"]
  LED15 = smd LED [color="Red (633nm)" package="0603 [SMD]"]
  LED16 = smd LED [color="Red (633nm)" package="0603 [SMD]"]
  LED17 = smd LED [color="Red (633nm)" package="0603 [SMD]"]
  LED18 = smd LED [color="Red (633nm)" package="0603 [SMD]"]
  LED19 = smd LED [color="Red (633nm)" package="0603 [SMD]"]
  LED20 = smd LED [color="Red (633nm)" package="0603 [SMD]"]
  LED21 = smd LED [color="Red (633nm)" package="0603 [SMD]"]
  LED22 = smd LED [color="Red (633nm)" package="0603 [SMD]"]
  LED23 = smd LED [color="Red (633nm)" package="0603 [SMD]"]
  LED24 = smd LED [color="Red (633nm)" package="0603 [SMD]"]
  LED25 = smd LED [color="Red (633nm)" package="0603 [SMD]"]
  LED26 = smd LED [color="Red (633nm)" package="0603 [SMD]"]
  LED27 = smd LED [color="Red (633nm)" package="0603 [SMD]"]
  LED28 = smd LED [color="Red (633nm)" package="0603 [SMD]"]
  LED29 = smd LED [color="Red (633nm)" package="0603 [SMD]"]
  LED30 = smd LED [color="Red (633nm)" package="0603 [SMD]"]
  LED31 = smd LED [color="Red (633nm)" package="0603 [SMD]"]
  LED32 = smd LED [color="Red (633nm)" package="0603 [SMD]"]
  LED33 = smd LED [color="Red (633nm)" package="0603 [SMD]"]
  LED34 = smd LED [color="Red (633nm)" package="0603 [SMD]"]
  LED35 = smd LED [color="Red (633nm)" package="0603 [SMD]"]
  LED36 = smd LED [color="Red (633nm)" package="0603 [SMD]"]
  LED37 = smd LED [color="Red (633nm)" package="0603 [SMD]"]
  LED38 = smd LED [color="Red (633nm)" package="0603 [SMD]"]
  LED39 = smd LED [color="Red (633nm)" package="0603 [SMD]"]
  LED40 = smd LED [color="Red (633nm)" package="0603 [SMD]"]
  LED41 = smd LED [color="Red (633nm)" package="0603 [SMD]"]
  LED42 = smd LED [color="Red (633nm)" package="0603 [SMD]"]
  LED43 = smd LED [color="Red (633nm)" package="0603 [SMD]"]
  LED44 = smd LED [color="Red (633nm)" package="0603 [SMD]"]
  LED45 = smd LED [color="Red (633nm)" package="0603 [SMD]"]
  LED46 = smd LED [color="Red (633nm)" package="0603 [SMD]"]
  LED47 = smd LED [color="Red (633nm)" package="0603 [SMD]"]
  LED48 = smd LED [color="Red (633nm)" package="0603 [SMD]"]
  LED49 = smd LED [color="Red (633nm)" package="0603 [SMD]"]
  LED50 = smd LED [color="Red (633nm)" package="0603 [SMD]"]
  LED51 = smd LED [color="Red (633nm)" package="0603 [SMD]"]
  LED52 = smd LED [color="Red (633nm)" package="0603 [SMD]"]
  LED53 = smd LED [color="Red (633nm)" package="0603 [SMD]"]
  LED54 = smd LED [color="Red (633nm)" package="0603 [SMD]"]
  LED55 = smd LED [color="Red (633nm)" package="0603 [SMD]"]
  LED56 = smd LED [color="Red (633nm)" package="0603 [SMD]"]
  LED57 = smd LED [color="Red (633nm)" package="0603 [SMD]"]
  LED58 = smd LED [color="Red (633nm)" package="0603 [SMD]"]
  LED59 = smd LED [color="Red (633nm)" package="0603 [SMD]"]
  LED60 = smd LED [color="Red (633nm)" package="0603 [SMD]"]
  LED61 = smd LED [color="Red (633nm)" package="0603 [SMD]"]
  LED62 = smd LED [color="Red (633nm)" package="0603 [SMD]"]
  LED63 = smd LED [color="Red (633nm)" package="0603 [SMD]"]
  LED64 = smd LED [color="Red (633nm)" package="0603 [SMD]"]

nets:
  N1: LED1.cathode, LED9.cathode, LED17.cathode, LED27.cathode, LED33.cathode, LED41.cathode, LED49.cathode, LED57.cathode
  N2: LED1.anode, LED2.anode, LED3.anode, LED4.anode, LED5.anode, LED6.anode, LED7.anode, LED8.anode
  N3: LED2.cathode, LED10.cathode, LED18.cathode, LED28.cathode, LED34.cathode, LED42.cathode, LED50.cathode, LED58.cathode
  N4: LED3.cathode, LED11.cathode, LED19.cathode, LED25.cathode, LED36.cathode, LED43.cathode, LED51.cathode, LED59.cathode
  N5: LED4.cathode, LED12.cathode, LED20.cathode, LED29.cathode, LED35.cathode, LED44.cathode, LED52.cathode, LED60.cathode
  N6: LED5.cathode, LED13.cathode, LED21.cathode, LED32.cathode, LED38.cathode, LED45.cathode, LED53.cathode, LED61.cathode
  N7: LED6.cathode, LED14.cathode, LED22.cathode, LED31.cathode, LED37.cathode, LED46.cathode, LED54.cathode, LED62.cathode
  N8: LED7.cathode, LED15.cathode, LED23.cathode, LED30.cathode, LED40.cathode, LED47.cathode, LED55.cathode, LED63.cathode
  N9: LED8.cathode, LED16.cathode, LED24.cathode, LED26.cathode, LED39.cathode, LED48.cathode, LED56.cathode, LED64.cathode
  N10: LED9.anode, LED10.anode, LED11.anode, LED12.anode, LED13.anode, LED14.anode, LED15.anode, LED16.anode
  N11: LED17.anode, LED18.anode, LED19.anode, LED20.anode, LED21.anode, LED22.anode, LED23.anode, LED24.anode
  N12: LED25.anode, LED26.anode, LED27.anode, LED28.anode, LED29.anode, LED30.anode, LED31.anode, LED32.anode
  N13: LED33.anode, LED34.anode, LED35.anode, LED36.anode, LED37.anode, LED38.anode, LED39.anode, LED40.anode
  N14: LED41.anode, LED42.anode, LED43.anode, LED44.anode, LED45.anode, LED46.anode, LED47.anode, LED48.anode
  N15: LED49.anode, LED50.anode, LED51.anode, LED52.anode, LED53.anode, LED54.anode, LED55.anode, LED56.anode
  N16: LED57.anode, LED58.anode, LED59.anode, LED60.anode, LED61.anode, LED62.anode, LED63.anode, LED64.anode
